# Fritzing sketch Fritzing Circuit Example (saved by Fritzing 0.9.4)
breadboards: 1

parts:
  WeMos_D1_Mini1 = WeMos D1 Mini
  JACK1 = 2.1mm Barrel Jack with Terminal Block
  U1 = 4RelayModule  # not connected
  NEOPIXEL1 = Neopixel Strip -- Black (30/m) [part_number=1376]
  C1 = Electrolytic Capacitor [capacitance=1000μF package="1010 [SMD, electrolytic]"]

nets:
  5V: WeMos_D1_Mini1.5V, JACK1.POS, NEOPIXEL1.+5V, C1.+
  N1: WeMos_D1_Mini1.G, JACK1.NEG, NEOPIXEL1.GND, C1.-

notes:
  PIN Setting
  - D0 (GPIO 16): Relay 1
  - D1 (GPIO 5): Relay 2
  - D2 (GPIO 4): IR Remote
  - D3 (GPIO 0): Button / LED Clock (when used)
  - D4 (GPIO 2): Data / WS2812b Stripe
  - D5 (GPIO 14): DS18B20 / IF Temperature Mod
  - D6 (GPIO 12): Stripe Power Switch Mosfet
  - D7 (GPIO 13): Relay 3
  - D8 (GPIO 15): Relay 4

custom parts:
  4RelayModule: 4 relay arduino module SONGLE SRD05VDC-SL-C
  Neopixel Strip -- Black (30/m): These NeoPixel strips have 30 digitally-addressable pixel LEDs per meter and are very affordable and are only 12.5 mm wide, 10 mm if you remove the strip from the casing.
